// Logisim project DMux.circ as structural Verilog: 1 circuit, main circuit main
module main (
  input  in,
  input  sel,
  output a,
  output b
);

  wire not_1_out;

  not not_1 (not_1_out, sel);
  and and_1 (a, in, not_1_out);
  and and_2 (b, in, sel);
endmodule
