// Logisim project FullAdder.circ as structural Verilog
module add (
  input  a,
  input  b,
  input  cin,
  output sum,
  output cout
);

  wire and_1_out, and_2_out, and_3_out, and_4_out, and_5_out, and_6_out, and_7_out, not_1_out, not_2_out,
       not_3_out, not_4_out, not_5_out, not_6_out;

  not not_1 (not_1_out, a);
  not not_2 (not_2_out, b);
  not not_3 (not_3_out, a);
  not not_4 (not_4_out, cin);
  not not_5 (not_5_out, b);
  not not_6 (not_6_out, cin);
  and and_1 (and_1_out, b, cin);
  and and_2 (and_2_out, a, cin);
  and and_3 (and_3_out, a, b);
  and and_4 (and_4_out, not_1_out, not_2_out, cin);
  and and_5 (and_5_out, not_3_out, b, not_4_out);
  and and_6 (and_6_out, a, not_5_out, not_6_out);
  and and_7 (and_7_out, a, b, cin);
  ExactlyOne xor_1 (.out(cout), .in0(and_1_out), .in1(and_2_out), .in2(and_3_out));
  ExactlyOne xor_2 (.out(sum), .in0(and_4_out), .in1(and_5_out), .in2(and_6_out), .in3(and_7_out));
endmodule

module adder (
  input  a,
  input  b,
  input  cin,
  output sum,
  output cout
);

  wire and_1_out, and_2_out, and_3_out, and_4_out, and_5_out, and_6_out, and_7_out, and_8_out, and_9_out,
       and_10_out, and_11_out, not_1_out, not_2_out, not_3_out, not_4_out, not_5_out, not_6_out, or_1_out,
       or_3_out, or_4_out;

  not not_1 (not_1_out, a);
  not not_2 (not_2_out, b);
  not not_3 (not_3_out, a);
  not not_4 (not_4_out, b);
  and and_1 (and_1_out, b, cin);
  and and_2 (and_2_out, a, cin);
  and and_3 (and_3_out, not_1_out, not_2_out);
  and and_4 (and_4_out, not_3_out, b);
  not not_5 (not_5_out, cin);
  and and_5 (and_5_out, a, not_4_out);
  not not_6 (not_6_out, cin);
  and and_6 (and_6_out, a, b);
  or or_1 (or_1_out, and_1_out, and_2_out);
  and and_7 (and_7_out, a, b);
  and and_8 (and_8_out, and_3_out, cin);
  and and_9 (and_9_out, and_4_out, not_5_out);
  and and_10 (and_10_out, and_5_out, not_6_out);
  and and_11 (and_11_out, and_6_out, cin);
  or or_2 (cout, or_1_out, and_7_out);
  or or_3 (or_3_out, and_8_out, and_9_out);
  or or_4 (or_4_out, and_10_out, and_11_out);
  or or_5 (sum, or_3_out, or_4_out);
endmodule
