// Logisim project Not16.circ as structural Verilog: 1 circuit, main circuit main
module main (
  input  [15:0] in_1,
  output [15:0] out_2
);

  not not_1 (out_2[0], in_1[0]);
  not not_2 (out_2[4], in_1[4]);
  not not_3 (out_2[8], in_1[8]);
  not not_4 (out_2[12], in_1[12]);
  not not_5 (out_2[1], in_1[1]);
  not not_6 (out_2[2], in_1[2]);
  not not_7 (out_2[5], in_1[5]);
  not not_8 (out_2[6], in_1[6]);
  not not_9 (out_2[9], in_1[9]);
  not not_10 (out_2[10], in_1[10]);
  not not_11 (out_2[13], in_1[13]);
  not not_12 (out_2[14], in_1[14]);
  not not_13 (out_2[3], in_1[3]);
  not not_14 (out_2[7], in_1[7]);
  not not_15 (out_2[11], in_1[11]);
  not not_16 (out_2[15], in_1[15]);

  // Notes on the sheet:
  //   in
  //   out
endmodule
