// Logisim project Or16.circ as structural Verilog: 1 circuit, main circuit main
module main (
  input  [15:0] in_1,
  input  [15:0] in_2,
  output [15:0] out_3
);

  wire nand_1_out, nand_2_out, nand_3_out, nand_4_out, nand_5_out, nand_6_out, nand_7_out, nand_8_out,
       nand_9_out, nand_10_out, nand_11_out, nand_12_out, nand_13_out, nand_14_out, nand_15_out, nand_16_out,
       nand_17_out, nand_18_out, nand_19_out, nand_20_out, nand_21_out, nand_22_out, nand_23_out,
       nand_24_out, nand_25_out, nand_26_out, nand_27_out, nand_28_out, nand_29_out, nand_30_out,
       nand_31_out, nand_32_out;

  nand nand_1 (nand_1_out, in_1[0], in_1[0]);
  nand nand_2 (nand_2_out, in_1[1], in_1[1]);
  nand nand_3 (nand_3_out, in_1[2], in_1[2]);
  nand nand_4 (nand_4_out, in_1[3], in_1[3]);
  nand nand_5 (nand_5_out, in_1[4], in_1[4]);
  nand nand_6 (nand_6_out, in_1[5], in_1[5]);
  nand nand_7 (nand_7_out, in_1[6], in_1[6]);
  nand nand_8 (nand_8_out, in_1[7], in_1[7]);
  nand nand_9 (nand_9_out, in_1[8], in_1[8]);
  nand nand_10 (nand_10_out, in_1[9], in_1[9]);
  nand nand_11 (nand_11_out, in_1[10], in_1[10]);
  nand nand_12 (nand_12_out, in_1[11], in_1[11]);
  nand nand_13 (nand_13_out, in_1[12], in_1[12]);
  nand nand_14 (nand_14_out, in_1[13], in_1[13]);
  nand nand_15 (nand_15_out, in_1[14], in_1[14]);
  nand nand_16 (nand_16_out, in_1[15], in_1[15]);
  nand nand_17 (nand_17_out, in_2[0], in_2[0]);
  nand nand_18 (nand_18_out, in_2[1], in_2[1]);
  nand nand_19 (nand_19_out, in_2[2], in_2[2]);
  nand nand_20 (nand_20_out, in_2[3], in_2[3]);
  nand nand_21 (nand_21_out, in_2[4], in_2[4]);
  nand nand_22 (nand_22_out, in_2[5], in_2[5]);
  nand nand_23 (nand_23_out, in_2[6], in_2[6]);
  nand nand_24 (nand_24_out, in_2[7], in_2[7]);
  nand nand_25 (nand_25_out, in_2[8], in_2[8]);
  nand nand_26 (nand_26_out, in_2[9], in_2[9]);
  nand nand_27 (nand_27_out, in_2[10], in_2[10]);
  nand nand_28 (nand_28_out, in_2[11], in_2[11]);
  nand nand_29 (nand_29_out, in_2[12], in_2[12]);
  nand nand_30 (nand_30_out, in_2[13], in_2[13]);
  nand nand_31 (nand_31_out, in_2[14], in_2[14]);
  nand nand_32 (nand_32_out, in_2[15], in_2[15]);
  nand nand_33 (out_3[0], nand_1_out, nand_17_out);
  nand nand_34 (out_3[1], nand_2_out, nand_18_out);
  nand nand_35 (out_3[2], nand_3_out, nand_19_out);
  nand nand_36 (out_3[3], nand_4_out, nand_20_out);
  nand nand_37 (out_3[4], nand_5_out, nand_21_out);
  nand nand_38 (out_3[5], nand_6_out, nand_22_out);
  nand nand_39 (out_3[6], nand_7_out, nand_23_out);
  nand nand_40 (out_3[7], nand_8_out, nand_24_out);
  nand nand_41 (out_3[8], nand_9_out, nand_25_out);
  nand nand_42 (out_3[9], nand_10_out, nand_26_out);
  nand nand_43 (out_3[10], nand_11_out, nand_27_out);
  nand nand_44 (out_3[11], nand_12_out, nand_28_out);
  nand nand_45 (out_3[12], nand_13_out, nand_29_out);
  nand nand_46 (out_3[13], nand_14_out, nand_30_out);
  nand nand_47 (out_3[14], nand_15_out, nand_31_out);
  nand nand_48 (out_3[15], nand_16_out, nand_32_out);

  // Notes on the sheet:
  //   a
  //   b
  //   out
endmodule
