// Logisim project Xor.circ as structural Verilog: 1 circuit, main circuit main
module main (
);


  // Notes on the sheet:
  //   |  a  |  b  | out |
  //   |  0  |  0  |  0  |
  //   |  0  |  1  |  1  |
  //   |  1  |  0  |  1  |
  //   |  1  |  1  |  0  |
endmodule
